// Digital circuit cpu-real.dig as structural Verilog
module cpu_real (
  input  Manual_clk,
  input  Clk_toggle,
  input  clock
);

  wire _7408_1_pin2, _7408_1_pin3, _7408_1_pin6, AI, AO, CLK, MAI;
  wire [3:0] _74377_1_pin3, _74377_1_pin13;
  wire [7:0] a, b, mar;

  // _28c16 _28c16_1: pin names not known; wires that end beside it: 1'b1, 1'b0, 1'b0, 1'b0, 1'b0
  _74377 _74377_1 (
    .pin1(MAI), .pin2(mar[0]), .pin3(_74377_1_pin3[0]), .pin4(_74377_1_pin3[1]), .pin5(mar[1]),
    .pin6(mar[2]), .pin7(_74377_1_pin3[2]), .pin8(_74377_1_pin3[3]), .pin9(mar[3]), .pin10(1'b0),
    .pin11(CLK), .pin12(mar[4]), .pin13(_74377_1_pin13[0]), .pin14(_74377_1_pin13[1]), .pin15(mar[5]),
    .pin16(mar[6]), .pin17(_74377_1_pin13[2]), .pin18(_74377_1_pin13[3]), .pin19(mar[7]), .pin20(1'b1));
  // _74245 _74245_1: pin names not known; wires that end beside it: 1'b0, 1'b1, 1'b0
  _7408 _7408_1 (
    .pin1(Manual_clk), .pin2(_7408_1_pin2), .pin3(_7408_1_pin3), .pin4(Clk_toggle), .pin5(clock),
    .pin6(_7408_1_pin6), .pin7(1'b0), .pin14(1'b1));  // open: pin8, pin9, pin10, pin11, pin12, pin13
  _7432 _7432_1 (
    .pin7(1'b0), .pin8(CLK), .pin9(_7408_1_pin3), .pin10(_7408_1_pin6), .pin14(1'b1));  // open: pin1, pin2, pin3, pin4, pin5, pin6, pin11, pin12, pin13
  // _7404 _7404_1: pin names not known; wires that end beside it: 1'b0, _7408_1_pin2, Clk_toggle, 1'b1
  // _74245 _74245_2: pin names not known; wires that end beside it: 1'b1, 1'b1, AO, 1'b0
  _74377 _74377_2 (
    .pin1(MAI), .pin2(b[0]), .pin3(_74377_1_pin3[0]), .pin4(_74377_1_pin3[1]), .pin5(b[1]), .pin6(b[2]),
    .pin7(_74377_1_pin3[2]), .pin8(_74377_1_pin3[3]), .pin9(b[3]), .pin10(1'b0), .pin11(CLK), .pin12(b[4]),
    .pin13(_74377_1_pin13[0]), .pin14(_74377_1_pin13[1]), .pin15(b[5]), .pin16(b[6]),
    .pin17(_74377_1_pin13[2]), .pin18(_74377_1_pin13[3]), .pin19(b[7]), .pin20(1'b1));
  _74377 _74377_3 (
    .pin1(AI), .pin2(a[0]), .pin3(_74377_1_pin3[0]), .pin4(_74377_1_pin3[1]), .pin5(a[1]), .pin6(a[2]),
    .pin7(_74377_1_pin3[2]), .pin8(_74377_1_pin3[3]), .pin9(a[3]), .pin10(1'b0), .pin11(CLK), .pin12(a[4]),
    .pin13(_74377_1_pin13[0]), .pin14(_74377_1_pin13[1]), .pin15(a[5]), .pin16(a[6]),
    .pin17(_74377_1_pin13[2]), .pin18(_74377_1_pin13[3]), .pin19(a[7]), .pin20(1'b1));

  // Notes on the sheet:
  //   clock: Hz: 100
  //   Memory Address Register
  //   Clock
  //   A Register
  //   B Register
endmodule
